// Logisim project mips-like.circ as structural Verilog: 4 circuits, main circuit PROCESSADOR
module PROCESSADOR (
  output [31:0] \INSTRUÇÃO 
);

  wire button_1_out, clock_1_out, UC_read_mer, UC_write_mer, UC_write_reg;
  wire [3:0] UC_ula_op;
  wire [31:0] adder_1_out, banco_de_registradores_1_r0_d, banco_de_registradores_1_r1_d,
       demultiplexer_1_out0, demultiplexer_1_out1, PC_q, ula_1_ula_out;

  Adder #(.width(32)) adder_1 (.a(PC_q), .b(32'h4), .out(adder_1_out));  // open: cin, cout
  Register #(.width(32)) PC (.D(adder_1_out), .Q(PC_q), .clk(clock_1_out), .clr(button_1_out));  // open: en
  Clock clock_1 (.out(clock_1_out));
  Button button_1 (.out(button_1_out));
  ROM #(.dataWidth(32)) rom_1 (.addr(PC_q[9:2]), .data(\INSTRUÇÃO ));  // open: sel
  UC UC (
    .write_reg(UC_write_reg), .ula_op(UC_ula_op), .E0(\INSTRUÇÃO [31]), .E1(\INSTRUÇÃO [30]),
    .E2(\INSTRUÇÃO [29]), .E3(\INSTRUÇÃO [28]), .read_mer(UC_read_mer), .write_mer(UC_write_mer));
  BANCO_DE_REGISTRADORES banco_de_registradores_1 (
    .DATA_WRITE(demultiplexer_1_out0), .CLK(clock_1_out), .RW(\INSTRUÇÃO [27:24]),
    .R0_D(banco_de_registradores_1_r0_d), .R0(\INSTRUÇÃO [19:16]), .R1_D(banco_de_registradores_1_r1_d),
    .R1(\INSTRUÇÃO [23:20]), .RW_2(UC_write_reg), .RESET(button_1_out));
  ULA ula_1 (
    .DATA_0(banco_de_registradores_1_r0_d), .DATA_1(banco_de_registradores_1_r1_d), .ULA_OUT(ula_1_ula_out),
    .ULA_OP(UC_ula_op));
  Demultiplexer #(.width(32), .enable("false")) demultiplexer_1 (
    .out0(demultiplexer_1_out0), .out1(demultiplexer_1_out1), .in(ula_1_ula_out), .sel(UC_read_mer));
  RAM #(.dataWidth(32)) ram_1 (
    .addr(demultiplexer_1_out1[7:0]), .data(demultiplexer_1_out0), .clk(clock_1_out), .ld(UC_read_mer));  // open: sel, clr

  // Notes on the sheet:
  //   REG_0
  //   REG_1
  //   REG_W
  //   contents of rom_1 (hex, n*v repeats v):
  //   ffffffff 0 0 0 11111111
  //   DATA_W
  //   BANCO DE REGISTRADORES
  //   REG0_D
  //   REG1_D
  //   ULA
endmodule

module ULA (
  input  [31:0] DATA_1,
  input  [31:0] DATA_0,
  input  [3:0] ULA_OP,
  output [31:0] ULA_OUT
);

  wire [31:0] adder_1_out, multiplier_1_out, subtractor_1_out;

  Adder #(.width(32)) adder_1 (.a(DATA_0), .b(DATA_1), .out(adder_1_out));  // open: cin, cout
  Subtractor #(.width(32)) subtractor_1 (.a(DATA_0), .b(DATA_1), .out(subtractor_1_out));  // open: bin, bout
  Multiplier #(.width(32)) multiplier_1 (.a(DATA_0), .b(DATA_1), .out(multiplier_1_out));  // open: cin, cout
  Multiplexer #(.select(4), .width(32), .enable("false")) multiplexer_1 (
    .in1(adder_1_out), .in2(subtractor_1_out), .in3(multiplier_1_out), .out(ULA_OUT), .sel(ULA_OP));  // open: in0, in4, in5, in6, in7, in8, in9, in10, in11, in12, in13, in14, in15
endmodule

module UC (
  input  E0,
  input  E1,
  input  E2,
  input  E3,
  output write_reg,
  output [3:0] ula_op,
  output read_mer,
  output write_mer
);

  and and_1 (read_mer, E2, E3);
  and and_2 (write_mer, read_mer, E0);

  assign ula_op = {E3, E2, E1, E0};
  assign write_reg = E3;
endmodule

module BANCO_DE_REGISTRADORES (
  input  [31:0] DATA_WRITE,
  input  [3:0] R0,
  input  CLK,
  input  [3:0] R1,
  input  [3:0] RW,
  input  RESET,
  input  RW_2,
  output [31:0] R0_D,
  output [31:0] R1_D
);

  wire demultiplexer_1_out0, demultiplexer_1_out1, demultiplexer_1_out2, demultiplexer_1_out3,
       demultiplexer_1_out4, demultiplexer_1_out5, demultiplexer_1_out6, demultiplexer_1_out7,
       demultiplexer_1_out8, demultiplexer_1_out9, demultiplexer_1_out10, demultiplexer_1_out11,
       demultiplexer_1_out12, demultiplexer_1_out13, demultiplexer_1_out14, demultiplexer_1_out15;
  wire [31:0] register_1_q, register_2_q, register_3_q, register_4_q, register_5_q, register_6_q,
       register_7_q, register_8_q, register_9_q, register_10_q, register_11_q, register_12_q, register_13_q,
       register_14_q, register_15_q, register_16_q;

  Demultiplexer #(.select(4), .enable("false")) demultiplexer_1 (
    .out0(demultiplexer_1_out0), .out1(demultiplexer_1_out1), .out2(demultiplexer_1_out2),
    .out3(demultiplexer_1_out3), .out4(demultiplexer_1_out4), .out5(demultiplexer_1_out5),
    .out6(demultiplexer_1_out6), .out7(demultiplexer_1_out7), .out8(demultiplexer_1_out8),
    .out9(demultiplexer_1_out9), .out10(demultiplexer_1_out10), .out11(demultiplexer_1_out11),
    .out12(demultiplexer_1_out12), .out13(demultiplexer_1_out13), .out14(demultiplexer_1_out14),
    .out15(demultiplexer_1_out15), .in(RW_2), .sel(RW));
  Register #(.width(32)) register_1 (
    .D(DATA_WRITE), .en(demultiplexer_1_out0), .Q(register_1_q), .clk(CLK), .clr(RESET));
  Register #(.width(32)) register_2 (
    .D(DATA_WRITE), .en(demultiplexer_1_out1), .Q(register_2_q), .clk(CLK), .clr(RESET));
  Register #(.width(32)) register_3 (
    .D(DATA_WRITE), .en(demultiplexer_1_out2), .Q(register_3_q), .clk(CLK), .clr(RESET));
  Register #(.width(32)) register_4 (
    .D(DATA_WRITE), .en(demultiplexer_1_out3), .Q(register_4_q), .clk(CLK), .clr(RESET));
  Register #(.width(32)) register_5 (
    .D(DATA_WRITE), .en(demultiplexer_1_out4), .Q(register_5_q), .clk(CLK), .clr(RESET));
  Register #(.width(32)) register_6 (
    .D(DATA_WRITE), .en(demultiplexer_1_out5), .Q(register_6_q), .clk(CLK), .clr(RESET));
  Register #(.width(32)) register_7 (
    .D(DATA_WRITE), .en(demultiplexer_1_out6), .Q(register_7_q), .clk(CLK), .clr(RESET));
  Register #(.width(32)) register_8 (
    .D(DATA_WRITE), .en(demultiplexer_1_out7), .Q(register_8_q), .clk(CLK), .clr(RESET));
  Register #(.width(32)) register_9 (
    .D(DATA_WRITE), .en(demultiplexer_1_out8), .Q(register_9_q), .clk(CLK), .clr(RESET));
  Register #(.width(32)) register_10 (
    .D(DATA_WRITE), .en(demultiplexer_1_out9), .Q(register_10_q), .clk(CLK), .clr(RESET));
  Register #(.width(32)) register_11 (
    .D(DATA_WRITE), .en(demultiplexer_1_out10), .Q(register_11_q), .clk(CLK), .clr(RESET));
  Register #(.width(32)) register_12 (
    .D(DATA_WRITE), .en(demultiplexer_1_out11), .Q(register_12_q), .clk(CLK), .clr(RESET));
  Register #(.width(32)) register_13 (
    .D(DATA_WRITE), .en(demultiplexer_1_out12), .Q(register_13_q), .clk(CLK), .clr(RESET));
  Register #(.width(32)) register_14 (
    .D(DATA_WRITE), .en(demultiplexer_1_out13), .Q(register_14_q), .clk(CLK), .clr(RESET));
  Register #(.width(32)) register_15 (
    .D(DATA_WRITE), .en(demultiplexer_1_out14), .Q(register_15_q), .clk(CLK), .clr(RESET));
  Register #(.width(32)) register_16 (
    .D(DATA_WRITE), .en(demultiplexer_1_out15), .Q(register_16_q), .clk(CLK), .clr(RESET));
  Multiplexer #(.select(4), .width(32), .disabled(0), .enable("false")) multiplexer_1 (
    .in0(register_1_q), .in1(register_2_q), .in2(register_3_q), .in3(register_4_q), .in4(register_5_q),
    .in5(register_6_q), .in6(register_7_q), .in7(register_8_q), .in8(register_9_q), .in9(register_10_q),
    .in10(register_11_q), .in11(register_12_q), .in12(register_13_q), .in13(register_14_q),
    .in14(register_15_q), .in15(register_16_q), .out(R0_D), .sel(R0));
  Multiplexer #(.select(4), .width(32), .enable("false")) multiplexer_2 (
    .in0(register_1_q), .in1(register_2_q), .in2(register_3_q), .in3(register_4_q), .in4(register_5_q),
    .in5(register_6_q), .in6(register_7_q), .in7(register_8_q), .in8(register_9_q), .in9(register_10_q),
    .in10(register_11_q), .in11(register_12_q), .in12(register_13_q), .in13(register_14_q),
    .in14(register_15_q), .in15(register_16_q), .out(R1_D), .sel(R1));
endmodule
